# Fritzing sketch modelo_fritzing (saved by Fritzing 0.9.3b)
breadboards: 1

parts:
  Componente1 = Arduino Uno (Rev3)
  LED2 = smd LED [color="Yellow (585nm)" package="0603 [SMD]"]
  LED3 = smd LED [color="Green (555nm)" package="0603 [SMD]"]
  LED4 = smd LED [color="Red (633nm)" package="0603 [SMD]"]
  J1 = Piezo Speaker
  R1 = Resistor [tolerance=±5% resistance=220 package=THT]
  R2 = Resistor [tolerance=±5% resistance=220 package=THT]
  R3 = Resistor [tolerance=±5% resistance=220 package=THT]

nets:
  N1: Componente1.D8, R1.Pin_1
  N2: Componente1.D9_PWM, R2.Pin_1
  N3: Componente1.D10_PWM/SS, R3.Pin_1
  N4: Componente1.D11_PWM/MOSI, J1.pin2
  N5: Componente1.GND, LED2.cathode, LED3.cathode, LED4.cathode, J1.pin1
  N6: LED2.anode, R2.Pin_0
  N7: LED3.anode, R1.Pin_0
  N8: LED4.anode, R3.Pin_0
